# Fritzing sketch uv_schematic_diagram (saved by Fritzing 0.8.7b)
circuit board: 8.46667cm x 5.64444cm
breadboards: 1

parts:
  S1 = H-Bridge with L298N
  M1 = DC Motor
  M2 = DC Motor
  Raspberry_Pi_1 = Raspberry Pi 3
  PIR1 = PIR sensor
  PIR2 = PIR sensor
  J1 = Piezo Speaker
  CAMERA1 = TTL Serial JPEG Camera  # not connected
  M3 = DC Motor
  M4 = DC Motor
  U1 = LIPO-2000mAh [package=lipo-2000]
  U2 = LIPO-2000mAh [package=lipo-2000]
  U3 = LIPO-2000mAh [package=lipo-2000]
  KY-1 = Keyes Relay [package=THT]
  KY-2 = Keyes Relay [package=THT]
  Part1 = SRF05 Ultrasonic Rangefinder
  Part2 = SRF05 Ultrasonic Rangefinder

nets:
  N1: S1.12V, U1.+
  GND: S1.GND, Raspberry_Pi_1.GND, PIR1.GND, J1.pin1, U3.-
  N2: S1.ENA, Raspberry_Pi_1.GPIO2
  N3: S1.IN1, Raspberry_Pi_1.GPIO3
  N4: S1.IN2, Raspberry_Pi_1.GIPO4
  N5: S1.IN3, Raspberry_Pi_1.GIPO27
  N6: S1.IN4, Raspberry_Pi_1.GIPO22
  N7: S1.ENB, Raspberry_Pi_1.GIPO17
  N8: S1.M1-01, M2.pin_2, M4.pin_2
  N9: S1.M1-02, M2.pin_1, M4.pin_1
  N10: S1.M2-02, M1.pin_1, M3.pin_1
  N11: Raspberry_Pi_1.GIPO5, J1.pin2
  N12: Raspberry_Pi_1.GIPO21, Part1.Echo
  N13: Raspberry_Pi_1.GIPO20, Part1.Trig
  N14: Raspberry_Pi_1.GIPO7, Part2.Echo
  N15: Raspberry_Pi_1.GIPO8, Part2.Trig
  N16: Raspberry_Pi_1.GIPO23, KY-2.signal
  N17: Raspberry_Pi_1.GIPO18, PIR2.SIG
  N18: Raspberry_Pi_1.GIPO15, PIR1.SIG
  N19: Raspberry_Pi_1.GIPO14, KY-1.signal
  N20: U1.-, U2.+
  N21: U2.-, U3.+
  N22: KY-1.power, KY-2.power
  N23: KY-1.ground, KY-2.ground
  VCC: Part1.VCC, Part2.VCC
  GND_2: Part1.GND, Part2.GND

notes:
  11.1v
  battery
  PIR
  front
  PIR
  back

custom parts:
  H-Bridge with L298N: h-bridge
  TTL Serial JPEG Camera: TTL Serial JPEG Camera with NTSC Out
  Keyes Relay: The Keyes 5V relay module is suitable for SCM development, home appliance control. It uses a 5V~12V TIL control signal which can control DC / AC signal.
